# Fritzing sketch Gardbot (saved by Fritzing 0.9.3b)
circuit board: 8.46667cm x 5.64444cm
breadboards: 1

parts:
  Real_Time_Clock = DS1302 [package="SO8 [SMD]"]
  Arduino = Arduino Mega 2560 (Rev3)
  SD_Card_Reader = MicroSD Card Module
  Buzzer = Piezo Speaker

nets:
  5V: Real_Time_Clock.+V, Arduino.5V, SD_Card_Reader.VCC
  GND: Real_Time_Clock.0V, Arduino.GND, SD_Card_Reader.GND, Buzzer.pin1
  N1: Real_Time_Clock.CE_-_Chip_Enable, Arduino.D5_PWM
  N2: Real_Time_Clock.I/O_-_SPI_Data_In/Out, Arduino.D6_PWM
  N3: Real_Time_Clock.SCLK_-_SPI_Clock, Arduino.D7_PWM
  N4: Arduino.D4_PWM, Buzzer.pin2
  N5: Arduino.D24, SD_Card_Reader.CS
  N6: Arduino.D50, SD_Card_Reader.MISO
  N7: Arduino.D51, SD_Card_Reader.MOSI
  N8: Arduino.D52, SD_Card_Reader.SCK
